# Fritzing sketch Buzzer (saved by Fritzing 0.9.3b)

parts:
  WeMos_D1_R1 = WeMos D1 R2
  J1 = Piezo Speaker
  R1 = TRIMPOT [package=trimpot_pth_s3_lock]

nets:
  N1: WeMos_D1_R1.D0, R1.CW
  N2: WeMos_D1_R1.GND, J1.pin1, R1.CCW
  N3: J1.pin2, R1.WIPER

custom parts:
  WeMos D1 R2: The D1 R2 is a mini wifi board based on the ESP-8266EX.
