# Fritzing sketch Distance (saved by Fritzing 0.9.3b)

parts:
  WeMos_D1_R1 = WeMos D1 R2
  hc-sr1 = hc-sr04

nets:
  N1: WeMos_D1_R1.D7, WeMos_D1_R1.D8/SS, hc-sr1.Trig
  N2: WeMos_D1_R1.D7/MOSI, hc-sr1.Echo
  GND: WeMos_D1_R1.GND, hc-sr1.GND
  5V: WeMos_D1_R1.RESET, WeMos_D1_R1.5V, hc-sr1.VCC

custom parts:
  WeMos D1 R2: The D1 R2 is a mini wifi board based on the ESP-8266EX.
