# Fritzing sketch Distance_OLED (saved by Fritzing 0.9.3b)

parts:
  WeMos_D1_R1 = WeMos D1 R2
  Squix1 = OLED 0.96" 128x64 I2C SSD1306
  hc-sr1 = hc-sr04

nets:
  N1: WeMos_D1_R1.D7, WeMos_D1_R1.D8/SS, hc-sr1.Trig
  N2: WeMos_D1_R1.D7/MOSI, hc-sr1.Echo
  N3: WeMos_D1_R1.D1/SCL, Squix1.SCL
  N4: WeMos_D1_R1.D2/SDA, Squix1.SCA
  VIN: WeMos_D1_R1.VIN, WeMos_D1_R1.GND#20, Squix1.GND
  N5: WeMos_D1_R1.GND#21, hc-sr1.GND
  3.3V: WeMos_D1_R1.5V#22, WeMos_D1_R1.3.3V, Squix1.VCC
  N6: WeMos_D1_R1.RESET, WeMos_D1_R1.5V#25, hc-sr1.VCC

custom parts:
  WeMos D1 R2: The D1 R2 is a mini wifi board based on the ESP-8266EX.
