# Fritzing sketch Infrared (saved by Fritzing 0.9.3b)

parts:
  WeMos_D1_R1 = WeMos D1 R2
  IR1 = TSOP312.., 314.. [package=THT]

nets:
  N1: WeMos_D1_R1.D7, IR1.GND
  N2: WeMos_D1_R1.GND, IR1.Vs
  N3: WeMos_D1_R1.5V, IR1.Data

notes:
  VS1838B

custom parts:
  WeMos D1 R2: The D1 R2 is a mini wifi board based on the ESP-8266EX.
